# Fritzing sketch SPI_Demo-circuit_diagram (saved by Fritzing 0.9.10b)
breadboards: 1

parts:
  Raspberry_Pi_1 = Raspberry Pi 3 [part_number=RPI-3-V1.2]
  LED3 = LED - 5mm [color="White (8000K)" current=0.030 package="5 mm [THT]"]
  LED4 = LED - 5mm [color="White (8000K)" current=0.030 package="5 mm [THT]"]
  LED5 = LED - 5mm [color="White (8000K)" current=0.030 package="5 mm [THT]"]
  R1 = Resistor [tolerance=±5% power=0.25 resistance=1000 package=THT]
  R4 = PHOTOCELL [package=photocell]
  R5 = Resistor [tolerance=±5% power=0.25 resistance=10000 package=THT]
  R6 = Resistor [tolerance=±5% power=0.25 resistance=1000 package=THT]
  R7 = Resistor [tolerance=±5% power=0.25 resistance=1000 package=THT]
  ADC1 = MCP3008 [package=dil16]

nets:
  3V3: Raspberry_Pi_1.3v3, Raspberry_Pi_1.3V3, R4.P$1, ADC1.VREF, ADC1.VDD
  N1: Raspberry_Pi_1.GPIO2, R7.Pin_0
  N2: Raspberry_Pi_1.GPIO3, R6.Pin_0
  N3: Raspberry_Pi_1.GIPO4, R1.Pin_0
  N4: Raspberry_Pi_1.GIPO10, ADC1.Din
  N5: Raspberry_Pi_1.GIPO9, ADC1.Dout
  N6: Raspberry_Pi_1.GIPO11, ADC1.CLK
  N7: Raspberry_Pi_1.GND, LED3.cathode, LED4.cathode, LED5.cathode, R5.Pin_0, ADC1.DGND, ADC1.AGND
  N8: Raspberry_Pi_1.GIPO8, ADC1.CS/SHDN
  N9: LED3.anode, R6.Pin_1
  N10: LED4.anode, R7.Pin_1
  N11: LED5.anode, R1.Pin_1
  N12: R4.P$2, R5.Pin_1, ADC1.CH7
